# Fritzing sketch StepperUno12V (saved by Fritzing 0.9.2b)

parts:
  Part1 = Arduino Uno (Rev3) - ICSP
  M2 = Stepper Motor - Bipolar
  Part2 = EasyDriver_v44
  12V = Power plug

nets:
  5V: Part1.5V, Part2.VCC
  N1: Part1.D2, Part2.STEP
  N2: Part1.D3_PWM, Part2.DIR
  N3: Part1.D4, Part2.MS1
  N4: Part1.D5_PWM, Part2.MS2
  N5: Part1.D6_PWM, Part2.ENABLE
  GND: Part1.GND, Part2.GND, 12V.GND
  VIN: Part1.VIN, Part2.V+, 12V.VCC
  N6: M2.A, Part2.OUT2A
  N7: M2.C, Part2.OUT2B
  N8: M2.B, Part2.OUT1A
  N9: M2.D, Part2.OUT1B
